// Logisim project CalculadoraHexa4Bits.circ as structural Verilog
module _1_2Soma (
  input  A0,
  input  B0,
  output S0,
  output Co0
);

  xor xor_1 (S0, A0, B0);
  and and_1 (Co0, A0, B0);
endmodule

module SomadorCompleto (
  input  Ci0,
  input  A0,
  input  B0,
  output S0,
  output Co0
);

  wire n1_2soma_1_co0, n1_2soma_1_s0, n1_2soma_2_co0;

  _1_2Soma u_1_2soma_1 (.A0(A0), .B0(B0), .S0(n1_2soma_1_s0), .Co0(n1_2soma_1_co0));
  or or_1 (Co0, n1_2soma_1_co0, n1_2soma_2_co0);
  _1_2Soma u_1_2soma_2 (.A0(n1_2soma_1_s0), .B0(Ci0), .S0(S0), .Co0(n1_2soma_2_co0));
endmodule

module Somador4Bits (
  input  \Ø ,
  input  A0,
  input  B0,
  input  A1,
  input  B1,
  input  A2,
  input  B2,
  input  A3,
  input  B3,
  output S0,
  output S1,
  output S2,
  output S3,
  output C03,
  output Overflow
);

  wire somadorcompleto_1_co0, somadorcompleto_2_co0, somadorcompleto_3_co0;

  SomadorCompleto somadorcompleto_1 (.Ci0(\Ø ), .A0(A0), .B0(B0), .Co0(somadorcompleto_1_co0), .S0(S0));
  SomadorCompleto somadorcompleto_2 (
    .Ci0(somadorcompleto_1_co0), .A0(A1), .B0(B1), .Co0(somadorcompleto_2_co0), .S0(S1));
  SomadorCompleto somadorcompleto_3 (
    .Ci0(somadorcompleto_2_co0), .A0(A2), .B0(B2), .Co0(somadorcompleto_3_co0), .S0(S2));
  SomadorCompleto somadorcompleto_4 (.Ci0(somadorcompleto_3_co0), .A0(A3), .B0(B3), .Co0(C03), .S0(S3));
  xor xor_1 (Overflow, C03, somadorcompleto_3_co0);
endmodule

module Decodificador (
  input  E0,
  input  E1,
  input  E2,
  input  E3,
  output A,
  output B,
  output C,
  output D,
  output E,
  output F,
  output G
);

  wire and_1_out, and_2_out, and_3_out, and_4_out, and_5_out, and_6_out, and_7_out, and_8_out, and_9_out,
       and_10_out, and_11_out, and_12_out, and_13_out, and_14_out, and_15_out, and_16_out, and_17_out,
       and_18_out, and_19_out, and_20_out, and_21_out, and_22_out, and_23_out, and_24_out, and_25_out,
       and_26_out, and_27_out, and_28_out, and_29_out, and_30_out, and_31_out, and_32_out, and_33_out,
       and_34_out, and_35_out, and_36_out, and_37_out, and_38_out, and_39_out, and_40_out, and_41_out,
       and_42_out, and_43_out, and_44_out, and_45_out, and_46_out, not_1_out, not_2_out, not_3_out,
       not_4_out, not_5_out, not_6_out, not_7_out, not_8_out, not_9_out, not_10_out, not_11_out, not_12_out,
       not_13_out, not_14_out, not_15_out, not_16_out, not_17_out, not_18_out, not_19_out, not_20_out,
       not_21_out, not_22_out, not_23_out, not_24_out, not_25_out, not_26_out, not_27_out, not_28_out,
       not_29_out, not_30_out, not_31_out, not_32_out, not_33_out, not_34_out, not_35_out, not_36_out,
       not_37_out, not_38_out, not_39_out, not_40_out, not_41_out, not_42_out, not_43_out, not_44_out,
       not_45_out, or_1_out, or_2_out, or_3_out, or_4_out, or_5_out, or_6_out, or_7_out, or_8_out, or_9_out,
       or_10_out, or_11_out, or_13_out, or_14_out, or_15_out, or_17_out, or_18_out, or_20_out, or_21_out,
       or_22_out, or_23_out;

  not not_1 (not_1_out, E0);
  not not_2 (not_2_out, E1);
  not not_3 (not_3_out, E0);
  and and_1 (and_1_out, not_3_out, not_4_out);
  not not_4 (not_4_out, E2);
  not not_5 (not_5_out, E3);
  not not_6 (not_6_out, E1);
  not not_7 (not_7_out, E3);
  not not_8 (not_8_out, E0);
  and and_2 (and_2_out, not_8_out, E2);
  not not_9 (not_9_out, E2);
  not not_10 (not_10_out, E0);
  and and_3 (and_3_out, not_10_out, not_11_out);
  not not_11 (not_11_out, E2);
  not not_12 (not_12_out, E0);
  and and_4 (and_4_out, not_12_out, E3);
  not not_13 (not_13_out, E2);
  not not_14 (not_14_out, E0);
  not not_15 (not_15_out, E1);
  not not_16 (not_16_out, E0);
  and and_5 (and_5_out, not_16_out, not_17_out);
  not not_17 (not_17_out, E1);
  not not_18 (not_18_out, E3);
  not not_19 (not_19_out, E1);
  and and_6 (and_6_out, not_19_out, E2);
  not not_20 (not_20_out, E2);
  not not_21 (not_21_out, E2);
  not not_22 (not_22_out, E1);
  and and_7 (and_7_out, not_22_out, not_23_out);
  not not_23 (not_23_out, E3);
  and and_8 (and_8_out, E2, not_24_out);
  not not_24 (not_24_out, E3);
  and and_9 (and_9_out, E0, E2);
  and and_10 (and_10_out, E0, E1);
  not not_25 (not_25_out, E0);
  and and_11 (and_11_out, not_25_out, not_26_out);
  not not_26 (not_26_out, E2);
  not not_27 (not_27_out, E3);
  not not_28 (not_28_out, E0);
  and and_12 (and_12_out, not_28_out, E1);
  not not_29 (not_29_out, E2);
  not not_30 (not_30_out, E0);
  not not_31 (not_31_out, E1);
  and and_13 (and_13_out, not_31_out, not_32_out);
  not not_32 (not_32_out, E3);
  not not_33 (not_33_out, E0);
  and and_14 (and_14_out, not_33_out, E2);
  not not_34 (not_34_out, E0);
  and and_15 (and_15_out, not_34_out, E1);
  and and_16 (and_16_out, E0, not_35_out);
  not not_35 (not_35_out, E1);
  not not_36 (not_36_out, E2);
  not not_37 (not_37_out, E1);
  and and_17 (and_17_out, not_37_out, E2);
  and and_18 (and_18_out, E1, not_38_out);
  not not_38 (not_38_out, E2);
  and and_19 (and_19_out, E1, not_39_out);
  not not_39 (not_39_out, E3);
  and and_20 (and_20_out, not_1_out, not_2_out);
  and and_21 (and_21_out, and_1_out, not_5_out);
  not not_40 (not_40_out, E1);
  not not_41 (not_41_out, E2);
  and and_22 (and_22_out, not_6_out, not_7_out);
  and and_23 (and_23_out, and_2_out, E3);
  and and_24 (and_24_out, E0, not_9_out);
  or or_1 (or_1_out, and_3_out, and_4_out);
  and and_25 (and_25_out, not_13_out, E3);
  and and_26 (and_26_out, not_14_out, E1);
  and and_27 (and_27_out, E0, not_15_out);
  and and_28 (and_28_out, and_5_out, not_18_out);
  and and_29 (and_29_out, and_6_out, E3);
  and and_30 (and_30_out, E1, not_20_out);
  and and_31 (and_31_out, E1, E2);
  not not_42 (not_42_out, E3);
  and and_32 (and_32_out, E0, not_21_out);
  not not_43 (not_43_out, E3);
  or or_2 (or_2_out, and_7_out, and_8_out);
  or or_3 (or_3_out, and_9_out, and_10_out);
  and and_33 (and_33_out, and_11_out, not_27_out);
  and and_34 (and_34_out, and_12_out, not_29_out);
  and and_35 (and_35_out, not_30_out, E1);
  not not_44 (not_44_out, E3);
  not not_45 (not_45_out, E1);
  or or_4 (or_4_out, and_13_out, and_14_out);
  and and_36 (and_36_out, and_15_out, E3);
  and and_37 (and_37_out, E1, E2);
  and and_38 (and_38_out, and_16_out, not_36_out);
  or or_5 (or_5_out, and_17_out, and_18_out);
  or or_6 (or_6_out, and_19_out, E0);
  or or_7 (or_7_out, and_20_out, and_21_out);
  and and_39 (and_39_out, not_40_out, not_41_out);
  or or_8 (or_8_out, and_22_out, and_23_out);
  and and_40 (and_40_out, and_24_out, E3);
  or or_9 (or_9_out, or_1_out, and_25_out);
  or or_10 (or_10_out, and_26_out, and_27_out);
  or or_11 (or_11_out, and_28_out, and_29_out);
  and and_41 (and_41_out, and_30_out, E3);
  and and_42 (and_42_out, and_31_out, not_42_out);
  and and_43 (and_43_out, and_32_out, not_43_out);
  or or_12 (D, or_2_out, or_3_out);
  or or_13 (or_13_out, and_33_out, and_34_out);
  and and_44 (and_44_out, and_35_out, not_44_out);
  and and_45 (and_45_out, E0, not_45_out);
  and and_46 (and_46_out, E0, E2);
  or or_14 (or_14_out, or_4_out, and_36_out);
  or or_15 (or_15_out, and_37_out, and_38_out);
  or or_16 (G, or_5_out, or_6_out);
  or or_17 (or_17_out, or_7_out, and_39_out);
  or or_18 (or_18_out, or_8_out, and_40_out);
  or or_19 (B, or_9_out, or_10_out);
  or or_20 (or_20_out, or_11_out, and_41_out);
  or or_21 (or_21_out, and_42_out, and_43_out);
  or or_22 (or_22_out, or_13_out, and_44_out);
  or or_23 (or_23_out, and_45_out, and_46_out);
  or or_24 (F, or_14_out, or_15_out);
  or or_25 (A, or_17_out, or_18_out);
  or or_26 (C, or_20_out, or_21_out);
  or or_27 (E, or_22_out, or_23_out);
endmodule

module Calculadora4Bits (
  input  A0,
  input  A1,
  input  A2,
  input  Ci,
  input  A3,
  input  B0,
  input  B1,
  input  B2,
  input  B3,
  output S0,
  output S1,
  output S2,
  output S3,
  output Co
);

  wire decodificador_1_a, decodificador_1_b, decodificador_1_c, decodificador_1_d, decodificador_1_e,
       decodificador_1_f, decodificador_1_g, decodificador_2_a, decodificador_2_b, decodificador_2_c,
       decodificador_2_d, decodificador_2_e, decodificador_2_f, decodificador_2_g, decodificador_3_a,
       decodificador_3_b, decodificador_3_c, decodificador_3_d, decodificador_3_e, decodificador_3_f,
       decodificador_3_g, somador4bits_1_overflow;

  Decodificador decodificador_1 (
    .E0(B0), .E1(B1), .E2(B2), .E3(B3), .A(decodificador_1_a), .B(decodificador_1_b), .C(decodificador_1_c),
    .D(decodificador_1_d), .E(decodificador_1_e), .F(decodificador_1_f), .G(decodificador_1_g));
  Decodificador decodificador_2 (
    .E0(A0), .E1(A1), .E2(A2), .E3(A3), .A(decodificador_2_a), .B(decodificador_2_b), .C(decodificador_2_c),
    .D(decodificador_2_d), .E(decodificador_2_e), .F(decodificador_2_f), .G(decodificador_2_g));
  Somador4Bits somador4bits_1 (
    .A0(A0), .B0(B0), .A1(A1), .B1(B1), .A2(A2), .B2(B2), .A3(A3), .B3(B3), .\Ø (Ci),
    .Overflow(somador4bits_1_overflow), .S0(S0), .S1(S1), .S2(S2), .S3(S3), .C03(Co));
  LED Led (.in(somador4bits_1_overflow));
  _7_Segment_Display u_7_segment_display_1 (
    .g(decodificador_2_g), .f(decodificador_2_e), .a(decodificador_2_f), .b(decodificador_2_a),
    .e(decodificador_2_d), .d(decodificador_2_c), .c(decodificador_2_b));  // open: dp
  _7_Segment_Display u_7_segment_display_2 (
    .g(decodificador_1_g), .f(decodificador_1_e), .a(decodificador_1_f), .b(decodificador_1_a),
    .e(decodificador_1_d), .d(decodificador_1_c), .c(decodificador_1_b));  // open: dp
  Decodificador decodificador_3 (
    .E0(S0), .E1(S1), .E2(S2), .E3(S3), .A(decodificador_3_a), .B(decodificador_3_b), .C(decodificador_3_c),
    .D(decodificador_3_d), .E(decodificador_3_e), .F(decodificador_3_f), .G(decodificador_3_g));
  _7_Segment_Display u_7_segment_display_3 (
    .g(decodificador_3_g), .f(decodificador_3_e), .a(decodificador_3_f), .b(decodificador_3_a),
    .e(decodificador_3_d), .d(decodificador_3_c), .c(decodificador_3_b));  // open: dp
endmodule
