// Logisim project Somadores.circ as structural Verilog: 3 circuits, main circuit 1/2Soma
module _1_2Soma (
  input  A0,
  input  B0,
  output S0,
  output Co0
);

  xor xor_1 (S0, A0, B0);
  and and_1 (Co0, A0, B0);
endmodule

module SomadorCompleto (
  input  Ci0,
  input  A0,
  input  B0,
  output S0,
  output Co0
);

  wire n1_2soma_1_co0, n1_2soma_1_s0, n1_2soma_2_co0;

  _1_2Soma u_1_2soma_1 (.A0(A0), .B0(B0), .S0(n1_2soma_1_s0), .Co0(n1_2soma_1_co0));
  or or_1 (Co0, n1_2soma_1_co0, n1_2soma_2_co0);
  _1_2Soma u_1_2soma_2 (.A0(n1_2soma_1_s0), .B0(Ci0), .S0(S0), .Co0(n1_2soma_2_co0));
endmodule

module Somador4Bits (
  input  \Ø ,
  input  A0,
  input  B0,
  input  A1,
  input  B1,
  input  A2,
  input  B2,
  input  A3,
  input  B3,
  output S0,
  output S1,
  output S2,
  output S3,
  output C03
);

  wire somadorcompleto_1_co0, somadorcompleto_2_co0, somadorcompleto_3_co0;

  SomadorCompleto somadorcompleto_1 (.Ci0(\Ø ), .A0(A0), .B0(B0), .Co0(somadorcompleto_1_co0), .S0(S0));
  SomadorCompleto somadorcompleto_2 (
    .Ci0(somadorcompleto_1_co0), .A0(A1), .B0(B1), .Co0(somadorcompleto_2_co0), .S0(S1));
  SomadorCompleto somadorcompleto_3 (
    .Ci0(somadorcompleto_2_co0), .A0(A2), .B0(B2), .Co0(somadorcompleto_3_co0), .S0(S2));
  SomadorCompleto somadorcompleto_4 (.Ci0(somadorcompleto_3_co0), .A0(A3), .B0(B3), .Co0(C03), .S0(S3));
endmodule
