// Logisim project ULAEPII.circ as structural Verilog
module Somador (
  input  Ci0,
  input  A0,
  input  B0,
  output S0,
  output Co0
);

  wire n1_2_somador_1_co, n1_2_somador_1_s, n1_2_somador_2_co;

  _1_2_somador u_1_2_somador_1 (.a(A0), .b(B0), .S(n1_2_somador_1_s), .Co(n1_2_somador_1_co));
  or or_1 (Co0, n1_2_somador_1_co, n1_2_somador_2_co);
  _1_2_somador u_1_2_somador_2 (.a(n1_2_somador_1_s), .b(Ci0), .S(S0), .Co(n1_2_somador_2_co));
endmodule

module _1_2_somador (
  input  a,
  input  b,
  output S,
  output Co
);

  and and_1 (Co, a, b);
  xor xor_1 (S, a, b);
endmodule

module Binvert (
  input  bi,
  input  b,
  input  nb,
  output S
);

  wire and_1_out, and_2_out, not_1_out;

  not not_1 (not_1_out, bi);
  and and_1 (and_1_out, not_1_out, b);
  and and_2 (and_2_out, bi, nb);
  or or_1 (S, and_1_out, and_2_out);
endmodule

module ULA (
  input  Bi,
  input  in_2,
  input  Op0,
  input  Op1,
  input  a,
  input  b,
  output out_7,
  output Co
);

  wire and_1_out, binvert_1_s, not_1_out, not_2_out, or_1_out, somador_1_s0;

  not not_1 (not_1_out, b);
  Binvert binvert_1 (.b(b), .nb(not_1_out), .bi(Bi), .S(binvert_1_s));
  and and_1 (and_1_out, a, b);
  or or_1 (or_1_out, a, b);
  not not_2 (not_2_out, a);
  Somador somador_1 (.Ci0(in_2), .A0(a), .B0(binvert_1_s), .Co0(Co), .S0(somador_1_s0));
  MUX mux_1 (.a(and_1_out), .b(or_1_out), .c(not_2_out), .d(somador_1_s0), .Op0(Op0), .Op1(Op1), .s(out_7));
endmodule

module MUX (
  input  Op0,
  input  Op1,
  input  a,
  input  b,
  input  c,
  input  d,
  output s
);

  wire and_1_out, and_2_out, and_3_out, and_4_out, not_1_out, not_2_out, not_3_out, not_4_out;

  and and_1 (and_1_out, a, not_1_out, not_2_out);
  not not_1 (not_1_out, Op0);
  not not_2 (not_2_out, Op1);
  and and_2 (and_2_out, b, Op1, not_3_out);
  not not_3 (not_3_out, Op0);
  not not_4 (not_4_out, Op1);
  and and_3 (and_3_out, c, not_4_out, Op0);
  and and_4 (and_4_out, d, Op0, Op1);
  ExactlyOne xor_1 (.out(s), .in0(and_1_out), .in1(and_2_out), .in2(and_3_out), .in3(and_4_out));
endmodule

module ULAde4Bits (
  input  Binvert,
  input  OP0,
  input  OP1,
  input  B3,
  input  B2,
  input  B1,
  input  B0,
  input  A3,
  input  A2,
  input  A1,
  input  A0,
  output S0,
  output S1,
  output S2,
  output S3,
  output Cout
);

  wire ula_1_co, ula_2_co, ula_3_co;

  ULA ula_1 (.a(A0), .b(B0), .Bi(Binvert), .in_2(Binvert), .Op0(OP0), .Op1(OP1), .out_7(S0), .Co(ula_1_co));
  ULA ula_2 (.a(A1), .b(B1), .Bi(Binvert), .in_2(ula_1_co), .Op0(OP0), .Op1(OP1), .out_7(S1), .Co(ula_2_co));
  ULA ula_3 (.a(A2), .b(B2), .Bi(Binvert), .in_2(ula_2_co), .Op0(OP0), .Op1(OP1), .out_7(S2), .Co(ula_3_co));
  ULA ula_4 (.a(A3), .b(B3), .Bi(Binvert), .in_2(ula_3_co), .Op0(OP0), .Op1(OP1), .out_7(S3), .Co(Cout));
endmodule
